# Fritzing sketch solardimmer (saved by Fritzing 0.9.10b)
breadboards: 1

parts:
  Mod1 = Amica NodeMCU DEVKIT 1.0
  Mod2 = Amica NodeMCU DEVKIT 1.0
  J1 = JST-B3P-VH [part_number=JST-B3P-VH package=THT]
  J2 = JST-VHR-3N [part_number=JST-VHR-3N package=THT]
  J3 = Screw terminal - 2 pins [package=THT]
  R1 = Resistor [tolerance=±5% power=0.25 resistance=680 package=THT]
  C1 = Ceramic Capacitor [capacitance=100nF voltage=35V package="100 mil [THT, multilayer]"]  # not connected
  C2 = Electrolytic Capacitor [capacitance=100µF voltage=35V package="100 mil [THT, electrolytic]"]  # not connected
  LED1 = LED - 3mm [color="Red (633nm)" current=0.030 package="3 mm [THT]"]  # not connected
  H1 = polarizedheader 4pin 0.156in [package=THT]
  R2 = Resistor [tolerance=±5% power=0.25 resistance=270 package=THT]
  R3 = Resistor [tolerance=±5% power=0.25 resistance=270 package=THT]
  R4 = Resistor [tolerance=±5% power=0.25 resistance=270 package=THT]
  H2 = polarizedheader 4pin 0.156in [package=THT]
  J4 = Camdenboss CTB0158-3 [part_number=CTB0158-3 package=THT]

nets:
  N1: Mod1.pin1, Mod1.pin_26, H1.pin4
  N2: Mod1.pin2, Mod1.pin_25, Mod1.pin_29, Mod2.pin2, Mod2.pin_29, J3.pin1, R1.Pin_0, H1.pin3, H2.pin2
  N3: Mod1.pin3, H1.pin2
  N4: Mod1.pin4, H1.pin1
  N5: Mod1.pin8, R4.Pin_0
  N6: Mod1.pin_13, R3.Pin_0
  N7: Mod1.pin_14, R2.Pin_0
  N8: Mod1.pin_30, Mod2.pin_30, J3.pin2
  N9: Mod2.pin1, Mod2.pin_26, H2.pin1
  N10: Mod2.pin6, H2.pin4
  N11: Mod2.pin7, H2.pin3
  N12: Mod2.pin8, R4.Pin_1
  N13: Mod2.pin_13, R3.Pin_1
  N14: Mod2.pin_14, R2.Pin_1
  N15: J1.pin2, J2.pin2, J2.pin_5, J4.pin3
  N16: J1.pin1, J2.pin1, J2.pin_4
  N17: J1.pin3, J4.pin2
  N18: J2.pin_6, J4.pin1

notes:
  L1
  N
  PE
  5P
  GND
  VCC
  TX
  RX
  IR-Lesekopf
  5V Netzteil
  RBDDimmer
  D1
  ZeroCross
  AC-N
  AC-L
  L-1
  230V Netzanschluss
  zum Heizstab
  Projekt: https://github.com/friedertonn/Nulleinspeisung   20.02.2023
  nur Schaltplan erstellt
